# Fritzing sketch sensors (saved by Fritzing 0.9.3b)
breadboards: 1

parts:
  Part1 = Arduino Ethernet Shield (Rev3)
  Part2 = Arduino Uno (Rev3)  # not connected
  R1 = Temperature Sensor (Thermistor) [thermistor_type=NTC package=THT]
  R2 = PHOTOCELL [package=photocell-kit]
  hc-sr1 = hc-sr04
  R3 = Resistor [tolerance=±5% resistance=10k package=THT]
  R4 = Resistor [tolerance=±5% resistance=10k package=THT]

nets:
  N1: Part1.A0, R2.P$1, R4.Pin_1
  N2: Part1.A5/SCL, R1.pin_0, R3.Pin_1
  N3: Part1.D2, hc-sr1.Echo
  N4: Part1.PWM_D3, hc-sr1.Trig
  5V: Part1.5V, R1.pin_1, R2.P$2, hc-sr1.VCC
  GND: Part1.GND, hc-sr1.GND, R3.Pin_0, R4.Pin_0
